// Logisim project cpu.circ as structural Verilog
module decompose (
  input  [5:0] in_1,
  input  [31:0] in_2
);

  wire comparator_1_eq, comparator_2_eq;

  Comparator #(.width(6)) comparator_1 (.a(in_2[5:0]), .b(in_1), .eq(comparator_1_eq));  // open: gt, lt
  // AND_Gate and_1 has open pins: in0=comparator_1_eq, in1=comparator_2_eq, out=open
  Comparator #(.width(6)) comparator_2 (.a(in_2[31:26]), .b({6{1'b0}}), .eq(comparator_2_eq));  // open: gt, lt

  // Other names for the same wires on the sheet: PCode[5:0] = in_2[5:0]
endmodule

module pc (
  input  clk,
  output [31:0] data
);

  wire [31:0] adder_1_out, register_1_q;

  Register #(.width(32)) register_1 (.D(adder_1_out), .Q(register_1_q), .clk(clk));  // open: en, clr
  Adder #(.width(32)) adder_1 (.a(32'h1), .b(register_1_q), .out(adder_1_out));  // open: cin, cout
  ROM rom_1 (.pos(register_1_q[23:0]), .data(data));  // open: sel
endmodule

module RAM (
  input  [23:0] pos,
  input  [31:0] data,
  input  sel,
  input  clk,
  input  ld,
  input  clr
);

  RAM_part #(.addrWidth(24), .dataWidth(32)) ram_1 (.addr(pos), .data(data), .sel(sel), .clk(clk), .ld(ld), .clr(clr));
endmodule

module ROM (
  input  [23:0] pos,
  input  sel,
  output [31:0] data
);

  ROM_part #(.addrWidth(24), .dataWidth(32)) rom_1 (.addr(pos), .data(data), .sel(sel));
endmodule
